// Digital circuit cpu_pipeline.dig as structural Verilog
module cpu_pipeline (
  input  Clock,
  input  _1,
  input  Reset,
  output dmem_re,
  output dmem_we,
  output [31:0] dmem_addr,
  output [31:0] imem_addr,
  output [31:0] dmem_wdata,
  output stall_debug,
  output [31:0] alu_debug,
  output [31:0] instr_debug,
  output flush_debug,
  output [31:0] pc_debug
);

  wire [31:0] ramdualport_1_d, ROM_d;

  top #(.applicationType("GHDL"), .ghdlOptions("--std=08 --workdir=/home/luiz-cavalini/AC-CPU-RV32I/digital"), .CodeFile("/home/luiz-cavalini/AC-CPU-RV32I/digital/top.vhd")) u_top (
    .clk_i(Clock), .rst_i(Reset), .imem_data_i(ROM_d), .dmem_rdata_i(ramdualport_1_d),
    .imem_addr_o(imem_addr), .dmem_addr_o(dmem_addr), .dmem_wdata_o(dmem_wdata), .dmem_we_o(dmem_we),
    .dmem_re_o(dmem_re), .pc_debug_o(pc_debug), .instr_debug_o(instr_debug), .alu_debug_o(alu_debug),
    .stall_debug_o(stall_debug), .flush_debug_o(flush_debug));
  ROM #(.AddrBits(8), .isProgramMemory("true"), .Bits(32)) ROM (.A(imem_addr[9:2]), .sel(_1), .D(ROM_d));
  RAMDualPort #(.AddrBits(8), .Bits(32)) ramdualport_1 (
    .A(dmem_addr[9:2]), .Din(dmem_wdata), .str(dmem_we), .C(Clock), .ld(dmem_re), .D(ramdualport_1_d));
  // also tied to GND on the sheet: {dmem_addr[0], dmem_addr[1], dmem_addr[10], dmem_addr[11], dmem_addr[12], dmem_addr[13], dmem_addr[14], dmem_addr[15], dmem_addr[16], dmem_addr[17], dmem_addr[18], dmem_addr[19], dmem_addr[20], dmem_addr[21], dmem_addr[22], dmem_addr[23], dmem_addr[24], dmem_addr[25], dmem_addr[26], dmem_addr[27], dmem_addr[28], dmem_addr[29], dmem_addr[30], dmem_addr[31], imem_addr[0], imem_addr[1], imem_addr[10], imem_addr[11], imem_addr[12], imem_addr[13], imem_addr[14], imem_addr[15], imem_addr[16], imem_addr[17], imem_addr[18], imem_addr[19], imem_addr[20], imem_addr[21], imem_addr[22], imem_addr[23], imem_addr[24], imem_addr[25], imem_addr[26], imem_addr[27], imem_addr[28], imem_addr[29], imem_addr[30], imem_addr[31]}

  // Notes on the sheet:
  //   contents of ROM (hex, n*v repeats v):
  //   500093,300113,2081b3,40208233
endmodule
